# Fritzing sketch 1 Sketch 2 (saved by Fritzing 0.9.3b)
breadboards: 1

parts:
  부품1 = Arduino Uno (Rev3)
  R1 = Resistor [tolerance=±5% resistance=220 package=THT]
  7_Segment1 = 7 Segment Display
  R2 = Resistor [tolerance=±5% resistance=220 package=THT]
  7_Segment2 = 7 Segment Display

nets:
  N1: 부품1.D8, 7_Segment1.Segment_G
  N2: 부품1.D12/MISO, R1.Pin_0, 7_Segment1.common_cathode
  N3: 부품1.D13/SCK, R2.Pin_0, 7_Segment2.common_cathode
  N4: 부품1.D2, 7_Segment2.Segment_C
  N5: 부품1.D3_PWM, 7_Segment2.Segment_D
  N6: 부품1.D4, 7_Segment2.Segment_E
  N7: 부품1.D5_PWM, 7_Segment1.Segment_B
  N8: 부품1.D6_PWM, 7_Segment1.Segment_A
  N9: R1.Pin_1, R2.Pin_1
